# Fritzing sketch Neopixel Camera Light (saved by Fritzing 0.9.3b)

parts:
  Part1 = 16 NeoPixel Ring [part_number=1463]
  Digispark1 = Digispark

nets:
  N1: Part1.IN, Digispark1.P2
  VDD: Part1.VDD, Digispark1.VCC
  GND: Part1.GND, Digispark1.GND

custom parts:
  16 NeoPixel Ring: 16 ultra bright smart LED NeoPixels are arranged in a circle with 1.75" (44.5mm) outer diameter. The rings are 'chainable' - connect the output pin of one to the input pin of another. Use only one microcontroller pin to control as many as you can chain together! Each LED is addressable as the driver chip is inside the LED. Each one has ~18mA constant current drive so the color will be very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
  Digispark: The Digispark is an Attiny85 based microcontroller development board similar to the Arduino line, only cheaper, smaller, and a bit less powerful. With a whole host of shields to extend its functionality and the ability to use the familiar Arduino IDE the Digispark is a great way to jump into electronics, or perfect for when an Arduino is too big or too much.
